// Logisim project haft_adder.circ as structural Verilog: 1 circuit, main circuit main
module main (
  input  Input_A,
  input  Input_B
);

  wire and_1_out, xor_1_out;

  xor xor_1 (xor_1_out, Input_B, Input_A);
  LED led_1 (.in(xor_1_out));
  and and_1 (and_1_out, Input_B, Input_A);
  LED led_2 (.in(and_1_out));

  // Notes on the sheet:
  //   XOR
  //   Sum
  //   Combine multiple haft-adder = full-adder
  //   HAFT-ADDER CIRCUIT
  //   Carry
  //   AND
  //   👀👀👀👀Author:
  //   Note:
  //   Sum = A ⊕ B (XOR)
  //   Carry = A ∧ B (AND)
  //   Biggest limitation:
  //   github - thinhNdang536
  //   Proceed only 2 inputs
  //   => cannot handle a carry-in
  //    from a previous stage.
  //   => yah, it can only work alone
endmodule
