// Logisim project d_flipflop_toggle.circ as structural Verilog: 1 circuit, main circuit main
module main (
);

  wire button_1_out, d_ff_1_q, d_ff_1_qn;

  Button button_1 (.out(button_1_out));
  D_Flip_Flop d_ff_1 (.D(d_ff_1_qn), .clk(button_1_out), .Q(d_ff_1_q), .Qn(d_ff_1_qn));  // open: preset, reset
  LED led_1 (.in(d_ff_1_q));
  LED led_2 (.in(d_ff_1_qn));

  // Notes on the sheet:
  //   Button
  //   D Flip-flop Status Toggle Circuit
  //   D Flip-flop
  //   Q
  //   Qi
  //   Notes:
  //   Qi: inverse of Q
  //   Author: thinhNdang0536
  //   Github: https://github.com/thinhNdang536
  //   How the circuit works:
  //   Button acts as one-time clock, provides a pulse to toggle D Flip-Flop each click time
  //   Qi acts as a input source with opposite signal of Q, to toggle status of Q
endmodule
