// Logisim project jk_truth_table.circ as structural Verilog: 1 circuit, main circuit main
module main (
);

  wire button_1_out, button_2_out, button_3_out, button_4_out, button_5_out, button_6_out, j_k_ff_1_q,
       j_k_ff_1_qn, j_k_ff_2_q, j_k_ff_2_qn, j_k_ff_3_q, j_k_ff_3_qn, j_k_ff_4_q, j_k_ff_4_qn;

  Button button_1 (.out(button_1_out));
  Button button_2 (.out(button_2_out));
  J_K_Flip_Flop j_k_ff_1 (
    .J(1'b0), .K(1'b0), .clk(button_1_out), .Q(j_k_ff_1_q), .Qn(j_k_ff_1_qn));  // open: preset, reset
  J_K_Flip_Flop j_k_ff_2 (
    .J(1'b1), .K(1'b1), .clk(button_2_out), .Q(j_k_ff_2_q), .Qn(j_k_ff_2_qn));  // open: preset, reset
  LED led_1 (.in(j_k_ff_1_q));
  LED led_2 (.in(j_k_ff_1_qn));
  LED led_3 (.in(j_k_ff_2_q));
  LED led_4 (.in(j_k_ff_2_qn));
  Button button_3 (.out(button_3_out));
  Button button_4 (.out(button_4_out));
  Button button_5 (.out(button_5_out));
  Button button_6 (.out(button_6_out));
  J_K_Flip_Flop j_k_ff_3 (
    .J(1'b1), .K(1'b0), .clk(button_3_out), .Q(j_k_ff_3_q), .Qn(j_k_ff_3_qn), .reset(button_4_out));  // open: preset
  J_K_Flip_Flop j_k_ff_4 (
    .J(1'b0), .K(1'b1), .clk(button_6_out), .Q(j_k_ff_4_q), .Qn(j_k_ff_4_qn), .preset(button_5_out));  // open: reset
  LED led_5 (.in(j_k_ff_3_q));
  LED led_6 (.in(j_k_ff_3_qn));
  LED led_7 (.in(j_k_ff_4_q));
  LED led_8 (.in(j_k_ff_4_qn));

  // Notes on the sheet:
  //   Author: thinhNdang0536
  //   Note:
  //   Qi: inverse of Q
  //   Truth table from circuit:
  //   J
  //   K
  //   CP
  //   J
  //   K
  //   CP
  //   Github: https://github.com/thinhNdang536
  //   J (Jump/Set): request to turn on Q on clock pulse 
  //   K (Kill/Reset): request to turn off Q on clock pulse 
  //   Q: stored bit of flipflop (0 or 1)
  //   Nobody requests to turn on or off Q?
  //   => Ok, I am not gonna do anything (unchange)
  //   J and K are fighting to change state of Q?
  //   CP (Clock Pulse): trigger that updates the flipflop state
  //   Unchange State
  //   Toggle State
  //   => Ok, I'm gonna change state respectively for fair (toggle)
  //   Q
  //   Q
  //   JK Flip-flop Circuit
  //   Qi
  //   Qi
  //   J
  //   K
  //   CP
  //   J
  //   K
  //   CP
  //   Press here to reset for testing
  //   (Force reset the flipflop)
  //   There is J requested to turn on Q?
  //   => Ok, I'm gonna set the stage of Q
  //   (Force set the flipflop)
  //   Press here to reset for testing
  //   There is K requested to turn off Q?
  //   => Ok, I'm gonna reset the state of Q
  //   S (Set override): force to turn on Q, regardless J and K
  //   R (Reset override): force to turn off Q, regardless J and K
  //   Set State
  //   Reset State
  //   Q
  //   Qi
  //   Q
  //   Qi
endmodule
